# Fritzing sketch Breadboard_Circuit (saved by Fritzing 0.9.9b)
breadboards: 1

parts:
  Mod1 = seeeduino-xiao
  Q1 = MOSFET-NCHANNEL [package=to220v]
  LED1 = LEDs [package=led10mm]
  BAT1 = 12 battery [package=battery]
  U1 = Mini-360 DC-DC Buck converter [package=THT]
  R1 = Resistor [tolerance=±1% resistance=1k package=THT]

nets:
  N1: Mod1.D8, Q1.G, R1.Pin_0
  N2: Mod1.GND, Q1.S, BAT1.-, U1.IN-, R1.Pin_1
  N3: Q1.D, LED1.A
  N4: LED1.C, U1.OUT+
  N5: BAT1.+, U1.IN+

custom parts:
  seeeduino-xiao: Seeeduino XIAO processor board.
  12 battery: 12V lead acid type battery, like the Husqvarna YTH2448 12V 35AH battery. This is the mini version 1/4 the size of the actual battery to be closer to typical breadboard parts (around 2in wide rathher than 7in). The pads in pcb are sized to accomidate up to 14ga wire (as these batterys will deliver high currents.)
  Mini-360 DC-DC Buck converter: Mini-360 DC-DC Buck converter. Tiny buck step down voltage converter, input voltage 4.75 to 23V output 1 to 17V adjustable. Available from ebay and the like.
